// Logisim project d_ff.circ as structural Verilog: 1 circuit, main circuit d_ff
module d_ff (
  input  d,
  input  clk,
  output q
);

  wire nand_1_out, nand_2_out, nand_3_out, nand_4_out, nand_5_out, nand_6_out, nand_7_out, nand_8_out,
       nand_10_out, not_1_out;

  nand nand_1 (nand_1_out, d, d);
  nand nand_2 (nand_2_out, d, not_1_out);
  nand nand_3 (nand_3_out, nand_1_out, not_1_out);
  not not_1 (not_1_out, clk);
  nand nand_4 (nand_4_out, nand_2_out, nand_5_out);
  nand nand_5 (nand_5_out, nand_4_out, nand_3_out);
  nand nand_6 (nand_6_out, nand_4_out, nand_4_out);
  nand nand_7 (nand_7_out, nand_4_out, clk);
  nand nand_8 (nand_8_out, nand_6_out, clk);
  nand nand_9 (q, nand_7_out, nand_10_out);
  nand nand_10 (nand_10_out, q, nand_8_out);

  // Notes on the sheet:
  //   MASTER: enabled when clk = 0
  //   Clock inverter
  //   SLAVE: enabled when clk = 1
endmodule
