// Logisim project d_ff_async.circ as structural Verilog: 1 circuit, main circuit d_ff_async
module d_ff_async (
  input  d,
  input  clk,
  input  set,
  input  clr,
  output q
);

  wire and_1_out, and_2_out, and_3_out, and_4_out, and_5_out, and_6_out, and_7_out, nor_1_out, nor_2_out,
       nor_4_out, not_1_out, not_2_out, not_3_out, not_4_out, not_5_out, or_1_out, or_2_out, or_3_out,
       or_4_out, or_5_out;

  not not_1 (not_1_out, clk);
  or or_1 (or_1_out, set, clr);
  not not_2 (not_2_out, clr);
  not not_3 (not_3_out, or_1_out);
  and and_1 (and_1_out, set, not_2_out);
  not not_4 (not_4_out, d);
  and and_2 (and_2_out, not_1_out, not_3_out);
  and and_3 (and_3_out, d, and_2_out);
  and and_4 (and_4_out, not_4_out, and_2_out);
  or or_2 (or_2_out, and_3_out, and_1_out);
  or or_3 (or_3_out, and_4_out, clr);
  nor nor_1 (nor_1_out, or_3_out, nor_2_out);
  nor nor_2 (nor_2_out, nor_1_out, or_2_out);
  not not_5 (not_5_out, nor_1_out);
  and and_5 (and_5_out, clk, not_3_out);
  and and_6 (and_6_out, nor_1_out, and_5_out);
  and and_7 (and_7_out, not_5_out, and_5_out);
  or or_4 (or_4_out, and_6_out, and_1_out);
  or or_5 (or_5_out, and_7_out, clr);
  nor nor_3 (q, or_5_out, nor_4_out);
  nor nor_4 (nor_4_out, q, or_4_out);

  // Notes on the sheet:
  //   Async control: Clear has priority
  //   run = NOT(set OR clr)
  //   effective_set = set AND NOT(clr)
  //   MASTER: clk = 0
  //   SLAVE: clk = 1
endmodule
