// Logisim project d_latch.circ as structural Verilog: 1 circuit, main circuit d_latch
module d_latch (
  input  d,
  input  en,
  output q
);

  wire nand_1_out, nand_2_out, nand_3_out, nand_5_out;

  nand nand_1 (nand_1_out, d, d);
  nand nand_2 (nand_2_out, d, en);
  nand nand_3 (nand_3_out, nand_1_out, en);
  nand nand_4 (q, nand_2_out, nand_5_out);
  nand nand_5 (nand_5_out, q, nand_3_out);

  // Notes on the sheet:
  //   D LATCH — NAND gates
  //   D inverter
  //   Cross-coupled storage
endmodule
