// Logisim project jk_ff.circ as structural Verilog: 1 circuit, main circuit jk_ff
module jk_ff (
  input  j,
  input  k,
  input  clk,
  input  clr_n,
  output q
);

  wire nand_1_out, nand_2_out, nand_3_out, nand_4_out, nand_5_out, nand_6_out, nand_7_out, nand_8_out,
       nand_9_out, nand_10_out, nand_11_out, nand_12_out, nand_13_out, nand_15_out;

  nand nand_1 (nand_1_out, k, k);
  nand nand_2 (nand_2_out, clk, clk);
  nand nand_3 (nand_3_out, j, nand_15_out);
  nand nand_4 (nand_4_out, nand_1_out, q);
  nand nand_5 (nand_5_out, nand_3_out, nand_4_out);
  nand nand_6 (nand_6_out, nand_5_out, nand_5_out);
  nand nand_7 (nand_7_out, nand_5_out, clr_n, nand_2_out);
  nand nand_8 (nand_8_out, nand_6_out, clr_n, nand_2_out);
  nand nand_9 (nand_9_out, nand_7_out, nand_10_out);
  nand nand_10 (nand_10_out, nand_9_out, clr_n, nand_8_out);
  nand nand_11 (nand_11_out, nand_9_out, nand_9_out);
  nand nand_12 (nand_12_out, nand_9_out, clr_n, clk);
  nand nand_13 (nand_13_out, nand_11_out, clr_n, clk);
  nand nand_14 (q, nand_12_out, nand_15_out);
  nand nand_15 (nand_15_out, q, clr_n, nand_13_out);

  // Notes on the sheet:
  //   JK next state: J.Qn + /K.Q
  //   START: clr_n = 0 resets Q. Click clr_n to 1 to RUN.
  //   Q and Qn feedback returns
  //   MASTER (clk = 0)
  //   SLAVE (clk = 1)
endmodule
