// Logisim project rs_latch.circ as structural Verilog: 1 circuit, main circuit rs_latch
module rs_latch (
  input  r,
  input  s,
  output q,
  output qn
);

  nor nor_1 (q, r, qn);
  nor nor_2 (qn, q, s);
endmodule
